# Fritzing sketch Tulip4 Breakout (saved by Fritzing 0.9.10b)
circuit board: 10.8045cm x 9.30846cm
breadboards: 1

parts:
  J2 = female pin header, 22 pins [form="♀ (female)"]
  Tulip4 = female pin header, 22 pins [form="♀ (female)"]
  USB = USB Connectors [package=usb-a-h]
  display = double row female pin header, 40 pins [form="♀ (female)"]
  audio = female pin header, 7 pins [form="♀ (female)"]
  R1 = Resistor [tolerance=±5% power=0.25 resistance=4.7k package=THT]
  R2 = Resistor [tolerance=±5% power=0.25 resistance=4.7k package=THT]
  MIDI = female pin header, 5 pins [form="♀ (female)"]

nets:
  N1: J2.pin1, display.pin19, MIDI.pin2
  N2: J2.pin2, R1.Pin_1, R2.Pin_0
  N3: J2.pin4, audio.pin1
  N4: J2.pin5, display.pin1
  N5: J2.pin6, display.pin16
  N6: J2.pin7, display.pin26
  N7: J2.pin8, display.pin15
  N8: J2.pin9, display.pin38
  N9: J2.pin10, display.pin2
  N10: J2.pin11, display.pin39, R1.Pin_0
  N11: J2.pin12, display.pin12, R2.Pin_1
  N12: J2.pin13, display.pin30
  N13: J2.pin14, display.pin11
  N14: J2.pin17, MIDI.pin5
  N15: J2.pin18, display.pin34
  N16: J2.pin20, display.pin6
  N17: J2.pin21, USB.VBUS, display.pin20, display.pin21, display.pin40, audio.pin4, audio.pin7, MIDI.pin3
  GND: J2.pin22, Tulip4.pin1, Tulip4.pin21, Tulip4.pin22, USB.GND, display.pin3, display.pin8, display.pin9, display.pin10, display.pin13, display.pin14, display.pin17, display.pin18, display.pin22, display.pin23, display.pin24, display.pin25, display.pin27, display.pin28, display.pin29, display.pin31, display.pin32, display.pin33, display.pin35, audio.pin6, MIDI.pin1
  N18: Tulip4.pin4, audio.pin2
  N19: Tulip4.pin5, audio.pin3
  N20: Tulip4.pin6, display.pin4
  N21: Tulip4.pin7, display.pin37
  N22: Tulip4.pin8, display.pin5
  N23: Tulip4.pin9, display.pin36
  N24: Tulip4.pin17, MIDI.pin4
  N25: Tulip4.pin18, display.pin7
  N26: Tulip4.pin19, USB.D+
  N27: Tulip4.pin20, USB.D-
